# Fritzing sketch schemat (saved by Fritzing 0.9.3b)

parts:
  Part2 = Black Joystick KY-023
  Part3 = Arduino Uno (Rev3) - ICSP
  Part4 = Matrix LED de 8x8 basada en MAX7219  # not connected

nets:
  N1: Part2.SW, Part3.D2
  N2: Part2.VRy, Part3.A0
  N3: Part2.VRx, Part3.A1
  N4: Part2.+5V, Part3.AREF
  GND: Part2.GND, Part3.GND

custom parts:
  Black Joystick KY-023: Description: The joystick is a combination of 2 analoog potentiometer and a digital switch. Arduino GND --> Module pin - Arduino +5V --> Module pin +5V Arduino Analoog 0 --> Module VRx Arduino Analoog 1 --> Module VRy Arduino Digital --> Module SW Dimensions: 1" x 1.25"
